# Fritzing sketch diagrama (saved by Fritzing 1.0.1rc)

parts:
  Grove1 = Grove OLED 128x96
  RE1 = KY-040 Rotary encoder [package=THT]
  KY-1 = Keyes Relay [package=THT]
  U1 = ESP32S-HiLetgo [part_number=ESP32S-HiLetgo]
  Pololu_A1 = Pololu A4988 [package=SO16]
  J1 = Screw terminal - 2 pins [package=THT]
  M1 = Stepper Motor - Bipolar
  IC1 = Voltage Regulator [package=78xxl]

nets:
  GND: Grove1.GND, RE1.GND, KY-1.ground, U1.GND, Pololu_A1.GND#8, IC1.GND
  VCC: Grove1.VCC, RE1.Vcc, KY-1.power, U1.3.3, Pololu_A1.RESET, Pololu_A1.SLEEP, Pololu_A1.VDD
  N1: Grove1.SDA, U1.GPIO21
  N2: Grove1.SCL, U1.GPIO22
  N3: RE1.SW, U1.GPIO5
  N4: RE1.DT, U1.GPIO19
  N5: RE1.CLK, U1.GPIO18
  N6: KY-1.signal, U1.GPIO32
  N7: U1.GPIO25, Pololu_A1.DIR
  N8: U1.GPIO26, Pololu_A1.STEP
  N9: U1.GPIO27, Pololu_A1.ENABLE
  N10: U1.GPIO14, Pololu_A1.MS1
  N11: U1.GPIO12, Pololu_A1.MS2
  N12: U1.GPIO13, Pololu_A1.MS3
  N13: U1.VIN, IC1.OUT
  N14: Pololu_A1.1B, M1.C
  N15: Pololu_A1.1A, M1.A
  N16: Pololu_A1.2A, M1.B
  N17: Pololu_A1.2B, M1.D
  N18: Pololu_A1.GND#14, J1.pin2
  N19: Pololu_A1.VMOT, J1.pin1, IC1.IN

custom parts:
  KY-040 Rotary encoder: KY-040 Rotary Encoder with switch on breakout borad from AZ Delivery
  Keyes Relay: The Keyes 5V relay module is suitable for SCM development, home appliance control. It uses a 5V~12V TIL control signal which can control DC / AC signal.
  ESP32S-HiLetgo: HiLetgo ESP-WROOM-32 ESP32 ESP-32S Development Board 2.4GHz Dual-Mode WiFi + Bluetooth Dual Cores Microcontroller The ESP32 integrated with Antenna switches, RF Balun, power amplifiers, low-noise amplifiers, filters, and management modules, and the entire solution occupies the least area of PCB. 2.4 GHz Wi-Fi plus Bluetooth dual-mode chip, with TSMC Ultra-low power consumption 40nm technology,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
